# Fritzing sketch Untitled Sketch (saved by Fritzing 0.9.3b)
breadboards: 1

parts:
  Часть1 = Arduino Mega 2560 (Rev3)
  Q1 = Basic FET N-Channel [package="D2Pak [SMD]"]
  Q2 = Basic FET N-Channel [package="D2Pak [SMD]"]
  Q3 = Basic FET N-Channel [package="D2Pak [SMD]"]
  Q4 = Basic FET N-Channel [package="D2Pak [SMD]"]
  R1 = Resistor [tolerance=±5% resistance=100 package=THT]
  R2 = Resistor [tolerance=±5% resistance=100 package=THT]
  R3 = Resistor [tolerance=±5% resistance=100 package=THT]
  R4 = Resistor [tolerance=±5% resistance=100 package=THT]
  R5 = Resistor [tolerance=±5% resistance=10k package=THT]
  R6 = Resistor [tolerance=±5% resistance=10k package=THT]
  R7 = Resistor [tolerance=±5% resistance=10k package=THT]
  R8 = Resistor [tolerance=±5% resistance=10k package=THT]

nets:
  N1: Часть1.GND, Q1.source, Q2.source, Q3.source, Q4.source, R5.Pin_0, R6.Pin_0, R7.Pin_0, R8.Pin_0
  N2: Часть1.D2_PWM, R4.Pin_1
  N3: Часть1.D3_PWM, R3.Pin_1
  N4: Часть1.D4_PWM, R2.Pin_1
  N5: Часть1.D5_PWM, R1.Pin_1
  N6: Q1.Gate, R1.Pin_0, R5.Pin_1
  N7: Q2.Gate, R3.Pin_0, R7.Pin_1
  N8: Q3.Gate, R4.Pin_0, R8.Pin_1
  N9: Q4.Gate, R2.Pin_0, R6.Pin_1

notes:
  Светодиодная лента
